// Digital circuit Two_Bit_ALU.dig as structural Verilog
module Two_Bit_ALU (
  input  A_1,
  input  A_0,
  input  B_1,
  input  B_0,
  input  [2:0] Control,
  output Y_0,
  output Y_1
);

  wire bitwise_and_1_y_0, bitwise_and_1_y_1, bitwise_xor_1_y_0, bitwise_xor_1_y_1, two_bit_comparator_1_y_0,
       two_bit_comparator_1_y_1, two_bit_divider_1_y_1, two_bit_multiplier_1_m_0, two_bit_multiplier_1_m_1,
       two_bit_parallel_adder_1_s_0, two_bit_parallel_adder_1_s_1;

  Bitwise_AND bitwise_and_1 (
    .A_1(A_1), .B_1(B_1), .A_0(A_0), .B_0(B_0), .Y_1(bitwise_and_1_y_1), .Y_0(bitwise_and_1_y_0));
  Two_Bit_Parallel_Adder two_bit_parallel_adder_1 (
    .A_0(A_0), .B_0(B_0), .A_1(A_1), .B_1(B_1), .S_0(two_bit_parallel_adder_1_s_0),
    .S_1(two_bit_parallel_adder_1_s_1));  // open: C_out
  Two_Bit_Multiplier two_bit_multiplier_1 (
    .A_0(A_0), .A_1(A_1), .B_0(B_0), .B_1(B_1), .M_0(two_bit_multiplier_1_m_0), .M_1(two_bit_multiplier_1_m_1));  // open: M_2, M_3
  Two_Bit_Divider two_bit_divider_1 (
    .A_0(A_0), .A_1(A_1), .B_0(B_0), .B_1(B_1), .Y_1(two_bit_divider_1_y_1), .Y_0(two_bit_multiplier_1_m_1));
  Two_Bit_Comparator two_bit_comparator_1 (
    .A_1(A_1), .B_1(B_1), .A_0(A_0), .B_0(B_0), .Y_0(two_bit_comparator_1_y_0), .Y_1(two_bit_comparator_1_y_1));
  Bitwise_XOR bitwise_xor_1 (
    .A_1(A_1), .B_1(B_1), .A_0(A_0), .B_0(B_0), .Y_1(bitwise_xor_1_y_1), .Y_0(bitwise_xor_1_y_0));
  Multiplexer #(.Selector_Bits(3)) multiplexer_1 (
    .sel(Control), .in_0(two_bit_parallel_adder_1_s_0), .in_1(two_bit_multiplier_1_m_0),
    .in_2(two_bit_multiplier_1_m_1), .in_3(two_bit_comparator_1_y_0), .in_4(bitwise_and_1_y_0),
    .in_5(bitwise_xor_1_y_0), .in_6(1'b0), .in_7(1'b0), .out(Y_0));
  Multiplexer #(.Selector_Bits(3)) multiplexer_2 (
    .sel(Control), .in_0(two_bit_parallel_adder_1_s_1), .in_1(two_bit_multiplier_1_m_1),
    .in_2(two_bit_divider_1_y_1), .in_3(two_bit_comparator_1_y_1), .in_4(bitwise_and_1_y_1),
    .in_5(bitwise_xor_1_y_1), .in_6(1'b0), .in_7(1'b0), .out(Y_1));

  // Notes on the sheet:
  //   0 = Addition
  //   1 = Multiplication
  //   2 = Division
  //   3 = Comparator
  //   4 = AND
  //   5 = XOR
endmodule
