// Digital circuit Two_Bit_Shift_Left.dig as structural Verilog
module Two_Bit_Shift_Left (
  input  In,
  input  Clk,
  output Y_1,
  output Y_0
);

  Neg_Edge_Triggered_D_FF neg_edge_triggered_d_ff_1 (.D(Y_0), .Clk(Clk), .Q(Y_1));  // open: nQ
  Neg_Edge_Triggered_D_FF neg_edge_triggered_d_ff_2 (.D(In), .Clk(Clk), .Q(Y_0));  // open: nQ
endmodule
